# Fritzing sketch WFduino102 (saved by Fritzing 0.9.3b)
breadboards: 1

parts:
  元件1 = Arduino Nano (Rev3.0)
  R1 = Resistor [tolerance=±5% resistance=220 package=THT]
  S1 = Pushbutton [package="[THT]"]
  LED1 = LEDs [package=led10mm]  # not connected

nets:
  N1: 元件1.GND, R1.Pin_0
  N2: 元件1.D11/MOSI, S1.Pin_3, S1.Pin_4
  N3: R1.Pin_1, S1.Pin_1, S1.Pin_2
